// Logisim project HALF ADDER USING XOR.circ as structural Verilog: 1 circuit, main circuit main
module main (
  input  A,
  input  B,
  output SUM,
  output CARRY
);

  xor \xor  (SUM, A, B);
  and \and  (CARRY, A, B);
endmodule
